# Fritzing sketch QlockTwo_Wemos_v0 (saved by Fritzing 0.9.3b)
circuit board: 8.46667cm x 5.64444cm
stripboards: 1

parts:
  WeMos_D1_Mini1 = WeMos D1 Mini
  V1 = DC Power [voltage=5]  # not connected
  U1 = DS3234 [package=ds3234]
  R1 = Photocell (LDR) [package=THT]
  R2 = Resistor [tolerance=±5% resistance=10k package=THT]
  S1 = Pushbutton [package="[THT]"]
  S2 = Pushbutton [package="[THT]"]
  S4 = Pushbutton [package="[THT]"]
  S3 = Pushbutton [package="[THT]"]
  R3 = Resistor [tolerance=±5% resistance=10k package=THT]
  R4 = Resistor [tolerance=±5% resistance=10k package=THT]
  R5 = Resistor [tolerance=±5% resistance=10k package=THT]
  R6 = Resistor [tolerance=±5% resistance=10k package=THT]
  LED_Strip = ws2812b [package="smd 2812b"]  # not connected
  C1 = Electrolytic Capacitor [capacitance=1µF package="100 mil [THT, electrolytic]"]
  Q1 = Basic FET N-Channel [package="TO220 [THT]"]  # not connected
  R7 = Resistor [tolerance=±5% resistance=10k package=THT]
  R8 = Resistor [tolerance=±5% resistance=10k package=THT]

nets (from the pcb view):
  3V3: WeMos_D1_Mini1.3V3, U1.VCC, R1.pin_0, S1.Pin_3, S1.Pin_4, S2.Pin_3, S2.Pin_4, S4.Pin_3, S4.Pin_4, S3.Pin_3, R8.Pin_1
  N1: WeMos_D1_Mini1.5V, C1.+, R7.Pin_1
  N2: WeMos_D1_Mini1.A0, R1.pin_1, R2.Pin_0
  N3: WeMos_D1_Mini1.D0, S1.Pin_1, S1.Pin_2, R3.Pin_0
  N4: WeMos_D1_Mini1.D1, U1.SCLK
  N5: WeMos_D1_Mini1.D2, U1.INT_SQW
  N6: WeMos_D1_Mini1.D3, R8.Pin_0
  N7: WeMos_D1_Mini1.D5, S2.Pin_1, S2.Pin_2, R4.Pin_0
  N8: WeMos_D1_Mini1.D6, S3.Pin_1, S3.Pin_2, R5.Pin_0
  N9: WeMos_D1_Mini1.D7, S4.Pin_1, S4.Pin_2, R6.Pin_0
  N10: WeMos_D1_Mini1.G, U1.GND, R2.Pin_1, R3.Pin_1, R4.Pin_1, R5.Pin_1, R6.Pin_1, C1.-

custom parts:
  Photocell (LDR): A generic light dependent resistor (LDR)
